# Fritzing sketch ballgame (saved by Fritzing 0.9.3b)
breadboards: 1

parts:
  U1 = ESP8266 WiFi Module [part_number=ESP8266]
  HC-SR04_Sensor_2 = HC-SR04 Ultrasonic Distance Sensor
  HC-SR04_Sensor_1 = HC-SR04 Ultrasonic Distance Sensor
  LED1 = LEDs [package=led10mm]
  R1 = Resistor [tolerance=±5% resistance=220 package="0805 [SMD]"]

nets:
  N1: U1.IO0, HC-SR04_Sensor_2.ECHO
  N2: U1.IO2, HC-SR04_Sensor_2.TRIG
  N3: U1.IO4, HC-SR04_Sensor_1.ECHO
  VCC: U1.3.3V#10, HC-SR04_Sensor_2.VCC, HC-SR04_Sensor_1.VCC
  GND: U1.GND#12, HC-SR04_Sensor_2.GND, HC-SR04_Sensor_1.GND, LED1.C
  N4: U1.IO5, HC-SR04_Sensor_1.TRIG
  N5: U1.IO13, R1.Pin_0
  N6: LED1.A, R1.Pin_1
